# Fritzing sketch Untitled Sketch (saved by Fritzing 1.0.1rc)
breadboards: 1

parts:
  A1 = drv-1012
  MH-ET_LIVE_ESP32_DEVKIT1 = MH-ET LIVE ESP32 DEVKIT 38 pins  # not connected

nets:
  N1: A1.Pin_1, A1.Pin_2, A1.Pin_4
  N2: A1.Pin_5, A1.Pin_6, A1.Pin_8
  N3: A1.Pin_10, A1.Pin_11, A1.Pin_12

custom parts:
  drv-1012: .The BTS7960 is a fully integrated high current H bridge module for motor drive applications.
  MH-ET LIVE ESP32 DEVKIT 38 pins: http://mh.nodebb.com/topic/2/mh-et-live-esp32-devkit
