# Fritzing sketch robot_motor_test (saved by Fritzing 1.0.1rc)
breadboards: 1

parts:
  A1 = drv-1012
  MH-ET_LIVE_ESP32_DEVKIT1 = MH-ET LIVE ESP32 DEVKIT 38 pins

nets (from the breadboard view):
  N1: A1.Pin_1, MH-ET_LIVE_ESP32_DEVKIT1.GND#64
  N2: A1.Pin_3, A1.Pin_5, A1.Pin_7, MH-ET_LIVE_ESP32_DEVKIT1.3V3
  N3: A1.Pin_4, MH-ET_LIVE_ESP32_DEVKIT1.IO26
  N4: A1.Pin_8, MH-ET_LIVE_ESP32_DEVKIT1.IO25

custom parts:
  drv-1012: .The BTS7960 is a fully integrated high current H bridge module for motor drive applications.
  MH-ET LIVE ESP32 DEVKIT 38 pins: http://mh.nodebb.com/topic/2/mh-et-live-esp32-devkit
